// Logisim project addition.circ as structural Verilog: 1 circuit, main circuit main
module main (
);

  wire and_1_out, and_2_out, and_3_out, and_4_out, and_5_out, and_6_out, and_7_out, and_8_out,
       dipswitch_1_p1, dipswitch_1_p2, dipswitch_1_p3, dipswitch_1_p4, dipswitch_1_p5, dipswitch_1_p6,
       dipswitch_1_p7, dipswitch_1_p8, or_1_out, or_2_out, or_3_out, or_4_out, xor_1_out, xor_2_out,
       xor_3_out, xor_4_out, xor_5_out, xor_6_out, xor_7_out, xor_8_out;

  // DipSwitch dipswitch_1: pin names not known; wires that end beside it: dipswitch_1_p1, dipswitch_1_p2, dipswitch_1_p3, dipswitch_1_p4, dipswitch_1_p5, dipswitch_1_p6, dipswitch_1_p7, dipswitch_1_p8
  LED led_1 (.in(dipswitch_1_p2));
  LED led_2 (.in(dipswitch_1_p1));
  LED led_3 (.in(dipswitch_1_p3));
  LED led_4 (.in(dipswitch_1_p4));
  xor xor_1 (xor_1_out, dipswitch_1_p2, dipswitch_1_p5);
  and and_1 (and_1_out, dipswitch_1_p2, dipswitch_1_p5);
  and and_2 (and_2_out, xor_1_out, 1'b0);
  xor xor_2 (xor_2_out, dipswitch_1_p1, dipswitch_1_p6);
  and and_3 (and_3_out, dipswitch_1_p1, dipswitch_1_p6);
  and and_4 (and_4_out, xor_2_out, or_2_out);
  LED led_5 (.in(dipswitch_1_p5));
  LED led_6 (.in(dipswitch_1_p6));
  LED led_7 (.in(dipswitch_1_p7));
  LED led_8 (.in(dipswitch_1_p8));
  or or_1 (or_1_out, and_3_out, and_4_out);
  xor xor_3 (xor_3_out, xor_1_out, 1'b0);
  or or_2 (or_2_out, and_1_out, and_2_out);
  xor xor_4 (xor_4_out, xor_2_out, or_2_out);
  xor xor_5 (xor_5_out, dipswitch_1_p3, dipswitch_1_p7);
  and and_5 (and_5_out, dipswitch_1_p3, dipswitch_1_p7);
  and and_6 (and_6_out, xor_5_out, or_1_out);
  xor xor_6 (xor_6_out, xor_5_out, or_1_out);
  or or_3 (or_3_out, and_5_out, and_6_out);
  xor xor_7 (xor_7_out, dipswitch_1_p4, dipswitch_1_p8);
  and and_7 (and_7_out, dipswitch_1_p4, dipswitch_1_p8);
  buf and_8 (and_8_out, or_3_out);  // AND_Gate
  xor xor_8 (xor_8_out, xor_7_out, or_3_out);
  or or_4 (or_4_out, and_7_out, and_8_out);
  LED led_9 (.in(xor_3_out));
  LED led_10 (.in(xor_4_out));
  LED led_11 (.in(xor_6_out));
  LED led_12 (.in(xor_8_out));
  LED led_13 (.in(or_4_out));

  // Notes on the sheet:
  //   From bottom to up
  //   1 - 4 is for first number, 5 - 8 is for second number
  //   from bottom to up
endmodule
